// Logisim project AQ2_graph.circ as structural Verilog: 3 circuits, main circuit 1-bit Full Adder
module _1_bit_Full_Adder (
  input  A,
  input  B,
  input  Cin,
  output Sum,
  output Cout
);

  wire nor_1_out, nor_2_out, nor_3_out, nor_4_out, nor_5_out, nor_6_out, nor_7_out;

  nor nor_1 (nor_1_out, A, B);
  nor nor_2 (nor_2_out, A, nor_1_out);
  nor nor_3 (nor_3_out, nor_1_out, B);
  nor nor_4 (nor_4_out, nor_2_out, nor_3_out);
  nor nor_5 (nor_5_out, nor_4_out, Cin);
  nor nor_6 (nor_6_out, nor_4_out, nor_5_out);
  nor nor_7 (nor_7_out, nor_5_out, Cin);
  nor nor_8 (Cout, nor_5_out, nor_1_out);
  nor nor_9 (Sum, nor_6_out, nor_7_out);
endmodule

module _4___bit_adder (
  input  A_0,
  input  B_0,
  input  A_1,
  input  B_1,
  input  A_2,
  input  B_2,
  input  A_3,
  input  B_3,
  output Sum_0,
  output Sum_0_2,
  output Sum_0_3,
  output Sum_0_4,
  output CarryOut
);

  wire n1_bit_full_adder_1_cout, n1_bit_full_adder_2_cout, n1_bit_full_adder_3_cout, nor_1_out, nor_2_out;

  nor nor_1 (nor_1_out, A_0, A_0);
  nor nor_2 (nor_2_out, A_0, nor_1_out);
  _1_bit_Full_Adder u_1_bit_full_adder_1 (
    .A(A_0), .B(B_0), .Sum(Sum_0), .Cin(nor_2_out), .Cout(n1_bit_full_adder_1_cout));
  _1_bit_Full_Adder u_1_bit_full_adder_2 (
    .A(A_1), .B(B_1), .Sum(Sum_0_2), .Cin(n1_bit_full_adder_1_cout), .Cout(n1_bit_full_adder_2_cout));
  _1_bit_Full_Adder u_1_bit_full_adder_3 (
    .A(A_2), .B(B_2), .Sum(Sum_0_3), .Cin(n1_bit_full_adder_2_cout), .Cout(n1_bit_full_adder_3_cout));
  _1_bit_Full_Adder u_1_bit_full_adder_4 (
    .A(A_3), .B(B_3), .Sum(Sum_0_4), .Cin(n1_bit_full_adder_3_cout), .Cout(CarryOut));
endmodule

module Hole (
  input  B_3,
  input  B_2,
  input  B_1,
  input  B_0,
  input  A_0,
  input  A_1,
  input  A_2,
  input  A_3,
  output P_0,
  output P_0_2,
  output P_0_3,
  output P_0_4,
  output P_0_5,
  output P_0_6,
  output P_0_7,
  output P_0_8
);

  wire n4_bit_adder_2_carryout, n4_bit_adder_2_sum_0_2, n4_bit_adder_2_sum_0_3, n4_bit_adder_2_sum_0_4,
       n4_bit_adder_3_carryout, n4_bit_adder_3_sum_0_2, n4_bit_adder_3_sum_0_3, n4_bit_adder_3_sum_0_4,
       nor_1_out, nor_2_out, nor_3_out, nor_4_out, nor_5_out, nor_6_out, nor_7_out, nor_8_out, nor_9_out,
       nor_10_out, nor_11_out, nor_12_out, nor_13_out, nor_14_out, nor_15_out, nor_16_out, nor_17_out,
       nor_18_out, nor_19_out, nor_20_out, nor_21_out, nor_22_out, nor_23_out, nor_24_out;

  nor nor_1 (nor_1_out, B_3, B_3);
  nor nor_2 (nor_2_out, A_0, A_0);
  nor nor_3 (nor_3_out, A_1, A_1);
  nor nor_4 (nor_4_out, A_2, A_2);
  nor nor_5 (nor_5_out, A_3, A_3);
  nor nor_6 (nor_6_out, B_2, B_2);
  nor nor_7 (nor_7_out, nor_5_out, nor_1_out);
  _4___bit_adder u_4_bit_adder_1 (
    .A_0(n4_bit_adder_2_sum_0_2), .B_0(nor_14_out), .A_1(n4_bit_adder_2_sum_0_3), .B_1(nor_9_out),
    .A_2(n4_bit_adder_2_sum_0_4), .B_2(nor_10_out), .A_3(n4_bit_adder_2_carryout), .B_3(nor_7_out),
    .Sum_0(P_0_5), .Sum_0_2(P_0_4), .Sum_0_3(P_0_3), .Sum_0_4(P_0_2), .CarryOut(P_0));
  nor nor_8 (nor_8_out, nor_4_out, nor_1_out);
  _4___bit_adder u_4_bit_adder_2 (
    .A_0(n4_bit_adder_3_sum_0_2), .B_0(nor_17_out), .A_1(n4_bit_adder_3_sum_0_3), .B_1(nor_12_out),
    .A_2(n4_bit_adder_3_sum_0_4), .B_2(nor_13_out), .A_3(n4_bit_adder_3_carryout), .B_3(nor_8_out),
    .Sum_0(P_0_6), .Sum_0_2(n4_bit_adder_2_sum_0_2), .Sum_0_3(n4_bit_adder_2_sum_0_3),
    .Sum_0_4(n4_bit_adder_2_sum_0_4), .CarryOut(n4_bit_adder_2_carryout));
  nor nor_9 (nor_9_out, nor_5_out, nor_18_out);
  nor nor_10 (nor_10_out, nor_5_out, nor_6_out);
  nor nor_11 (nor_11_out, nor_3_out, nor_1_out);
  _4___bit_adder u_4_bit_adder_3 (
    .A_0(nor_23_out), .B_0(nor_19_out), .A_1(nor_22_out), .B_1(nor_16_out), .A_2(nor_21_out),
    .B_2(nor_15_out), .A_3(nor_20_out), .B_3(nor_11_out), .Sum_0(P_0_7), .Sum_0_2(n4_bit_adder_3_sum_0_2),
    .Sum_0_3(n4_bit_adder_3_sum_0_3), .Sum_0_4(n4_bit_adder_3_sum_0_4), .CarryOut(n4_bit_adder_3_carryout));
  nor nor_12 (nor_12_out, nor_4_out, nor_18_out);
  nor nor_13 (nor_13_out, nor_4_out, nor_6_out);
  nor nor_14 (nor_14_out, nor_5_out, nor_24_out);
  nor nor_15 (nor_15_out, nor_3_out, nor_6_out);
  nor nor_16 (nor_16_out, nor_3_out, nor_18_out);
  nor nor_17 (nor_17_out, nor_4_out, nor_24_out);
  nor nor_18 (nor_18_out, B_1, B_1);
  nor nor_19 (nor_19_out, nor_3_out, nor_24_out);
  nor nor_20 (nor_20_out, A_0, nor_2_out);
  nor nor_21 (nor_21_out, nor_2_out, nor_1_out);
  nor nor_22 (nor_22_out, nor_2_out, nor_6_out);
  nor nor_23 (nor_23_out, nor_2_out, nor_18_out);
  nor nor_24 (nor_24_out, B_0, B_0);
  nor nor_25 (P_0_8, nor_2_out, nor_24_out);
endmodule
