// Logisim project AQ3_graph.circ as structural Verilog: 6 circuits, main circuit main
// Sum[0]
module main (
  input  C_0,
  input  A_0,
  input  B_0,
  input  A_1,
  input  B_1,
  input  A_2,
  input  B_2,
  input  A_3,
  input  B_3,
  output Sum_0,
  output C_1,
  output Sum_1,
  output C_2,
  output Sum_2,
  output C_3,
  output Sum_3,
  output C_4
);

  wire and_1_out, and_2_out, and_3_out, and_4_out, xor_1_out, xor_2_out, xor_3_out, xor_4_out;

  and and_1 (and_1_out, A_0, B_0);
  xor xor_1 (xor_1_out, A_0, B_0);
  and and_2 (and_2_out, A_1, B_1);
  xor xor_2 (xor_2_out, A_1, B_1);
  and and_3 (and_3_out, A_2, B_2);
  xor xor_3 (xor_3_out, A_2, B_2);
  and and_4 (and_4_out, A_3, B_3);
  xor xor_4 (xor_4_out, A_3, B_3);
  _4_bit_Carry_Look_Ahead u_4_bit_carry_look_ahead_1 (
    .C0(C_0), .G0(and_1_out), .P0(xor_1_out), .G1(and_2_out), .P1(xor_2_out), .G2(and_3_out), .P2(xor_3_out),
    .G3(and_4_out), .P3(xor_4_out), .C1(C_1), .C2(C_2), .C3(C_3), .C4(C_4));
  Full_Adder_by_NAND full_adder_by_nand_1 (.A(A_0), .B(B_0), .Cin(C_0), .Sum(Sum_0));
  Full_Adder_by_NAND full_adder_by_nand_2 (.A(A_1), .B(B_1), .Cin(C_1), .Sum(Sum_1));
  Full_Adder_by_NAND full_adder_by_nand_3 (.A(A_2), .B(B_2), .Cin(C_2), .Sum(Sum_2));
  Full_Adder_by_NAND full_adder_by_nand_4 (.A(A_3), .B(B_3), .Cin(C_3), .Sum(Sum_3));

  // Notes on the sheet:
  //   4-bit Carry Look Ahead Adder
  //   buttom
endmodule

module _4_bit_Carry_Look_Ahead (
  input  C0,
  input  G0,
  input  P0,
  input  G1,
  input  P1,
  input  G2,
  input  P2,
  input  G3,
  input  P3,
  output C1,
  output C2,
  output C3,
  output C4
);

  wire nand_1_out, nand_2_out, nand_3_out, nand_4_out, nand_5_out, nand_6_out, nand_7_out, nand_8_out,
       nand_9_out, nand_10_out, not_1_out, not_2_out, not_3_out, not_4_out;

  not not_1 (not_1_out, G0);
  nand nand_1 (nand_1_out, C0, P0);
  not not_2 (not_2_out, G1);
  nand nand_2 (nand_2_out, C0, P0, P1);
  nand nand_3 (nand_3_out, G0, P1);
  not not_3 (not_3_out, G2);
  nand nand_4 (nand_4_out, C0, P0, P1, P2);
  nand nand_5 (nand_5_out, G0, P1, P2);
  nand nand_6 (nand_6_out, G1, P2);
  not not_4 (not_4_out, G3);
  nand nand_7 (nand_7_out, C0, P0, P1, P2, P3);
  nand nand_8 (nand_8_out, G0, P1, P2, P3);
  nand nand_9 (nand_9_out, G1, P2, P3);
  nand nand_10 (nand_10_out, G2, P3);
  nand nand_11 (C1, not_1_out, nand_1_out);
  nand nand_12 (C2, not_2_out, nand_2_out, nand_3_out);
  nand nand_13 (C3, not_3_out, nand_4_out, nand_5_out, nand_6_out);
  nand nand_14 (C4, not_4_out, nand_7_out, nand_8_out, nand_9_out, nand_10_out);
endmodule

module Full_Adder_by_NAND (
  input  A,
  input  B,
  input  Cin,
  output Sum
);

  wire by_nand_out;

  xor by_nand (by_nand_out, A, B);
  xor by_nand_2 (Sum, by_nand_out, Cin);

  // Notes on the sheet:
  //   FullAdder by NAND
endmodule

module _2_to_4_decoder (
  input  in_0,
  input  in_1,
  input  Enable,
  output Out_0,
  output Out_0_2,
  output Out_0_3,
  output Out_0_4
);

  wire nand_1_out, nand_2_out;

  nand nand_1 (nand_1_out, in_0, in_0);
  nand nand_2 (nand_2_out, in_1, in_1);
  nand nand_3 (Out_0, nand_1_out, Enable, nand_2_out);
  nand nand_4 (Out_0_2, in_0, Enable, nand_2_out);
  nand nand_5 (Out_0_3, nand_1_out, Enable, in_1);
  nand nand_6 (Out_0_4, in_0, Enable, in_1);

  // Notes on the sheet:
  //   2 to 4 decoder output 0
endmodule

module _4_to_16_decoder (
  input  in_0,
  input  in_1,
  input  in_2,
  input  in_3,
  output Output_0,
  output Output_1,
  output Output_2,
  output Output_3,
  output Output_4,
  output Output_5,
  output Output_6,
  output Output_7,
  output Output_8,
  output Output_9,
  output Output_10,
  output Output_11,
  output Output_12,
  output Output_13,
  output Output_14,
  output Output_15
);

  wire n2_to_4_decoder_1_out_0, n2_to_4_decoder_1_out_0_2, n2_to_4_decoder_1_out_0_3,
       n2_to_4_decoder_1_out_0_4, not_1_out, not_2_out, not_3_out, not_4_out;

  _2_to_4_decoder u_2_to_4_decoder_1 (
    .in_0(in_2), .in_1(in_3), .Out_0(n2_to_4_decoder_1_out_0), .Out_0_2(n2_to_4_decoder_1_out_0_2),
    .Out_0_3(n2_to_4_decoder_1_out_0_3), .Out_0_4(n2_to_4_decoder_1_out_0_4), .Enable(1'b1));
  not not_1 (not_1_out, n2_to_4_decoder_1_out_0);
  not not_2 (not_2_out, n2_to_4_decoder_1_out_0_2);
  not not_3 (not_3_out, n2_to_4_decoder_1_out_0_3);
  not not_4 (not_4_out, n2_to_4_decoder_1_out_0_4);
  _2_to_4_decoder u_2_to_4_decoder_2 (
    .in_0(in_0), .in_1(in_1), .Out_0(Output_0), .Out_0_2(Output_1), .Out_0_3(Output_2), .Out_0_4(Output_3),
    .Enable(not_1_out));
  _2_to_4_decoder u_2_to_4_decoder_3 (
    .in_0(in_0), .in_1(in_1), .Out_0(Output_4), .Out_0_2(Output_5), .Out_0_3(Output_6), .Out_0_4(Output_7),
    .Enable(not_2_out));
  _2_to_4_decoder u_2_to_4_decoder_4 (
    .in_0(in_0), .in_1(in_1), .Out_0(Output_8), .Out_0_2(Output_9), .Out_0_3(Output_10), .Out_0_4(Output_11),
    .Enable(not_3_out));
  _2_to_4_decoder u_2_to_4_decoder_5 (
    .in_0(in_0), .in_1(in_1), .Out_0(Output_12), .Out_0_2(Output_13), .Out_0_3(Output_14),
    .Out_0_4(Output_15), .Enable(not_4_out));
endmodule

module _7___segment_display (
  input  in_0,
  input  in_1,
  input  in_2,
  input  in_3,
  output CA,
  output CB,
  output CC,
  output CD,
  output CE,
  output CF,
  output CG
);

  wire n4_to_16_decoder_1_output_0, n4_to_16_decoder_1_output_1, n4_to_16_decoder_1_output_2,
       n4_to_16_decoder_1_output_3, n4_to_16_decoder_1_output_4, n4_to_16_decoder_1_output_5,
       n4_to_16_decoder_1_output_6, n4_to_16_decoder_1_output_7, n4_to_16_decoder_1_output_8,
       n4_to_16_decoder_1_output_9, n4_to_16_decoder_1_output_10, n4_to_16_decoder_1_output_11,
       n4_to_16_decoder_1_output_12, n4_to_16_decoder_1_output_13, n4_to_16_decoder_1_output_14,
       n4_to_16_decoder_1_output_15, nand_1_out, nand_2_out, nand_3_out, nand_4_out, nand_5_out, nand_6_out,
       nand_7_out;

  nand nand_1 (nand_1_out, n4_to_16_decoder_1_output_0, n4_to_16_decoder_1_output_2, n4_to_16_decoder_1_output_3, n4_to_16_decoder_1_output_5, n4_to_16_decoder_1_output_6, n4_to_16_decoder_1_output_7, n4_to_16_decoder_1_output_8, n4_to_16_decoder_1_output_9, n4_to_16_decoder_1_output_10, n4_to_16_decoder_1_output_12, n4_to_16_decoder_1_output_14, n4_to_16_decoder_1_output_15);
  not not_1 (CA, nand_1_out);
  _4_to_16_decoder u_4_to_16_decoder_1 (
    .in_0(in_0), .in_1(in_1), .in_2(in_2), .in_3(in_3), .Output_0(n4_to_16_decoder_1_output_0),
    .Output_1(n4_to_16_decoder_1_output_1), .Output_2(n4_to_16_decoder_1_output_2),
    .Output_3(n4_to_16_decoder_1_output_3), .Output_4(n4_to_16_decoder_1_output_4),
    .Output_5(n4_to_16_decoder_1_output_5), .Output_6(n4_to_16_decoder_1_output_6),
    .Output_7(n4_to_16_decoder_1_output_7), .Output_8(n4_to_16_decoder_1_output_8),
    .Output_9(n4_to_16_decoder_1_output_9), .Output_10(n4_to_16_decoder_1_output_10),
    .Output_11(n4_to_16_decoder_1_output_11), .Output_12(n4_to_16_decoder_1_output_12),
    .Output_13(n4_to_16_decoder_1_output_13), .Output_14(n4_to_16_decoder_1_output_14),
    .Output_15(n4_to_16_decoder_1_output_15));
  nand nand_2 (nand_2_out, n4_to_16_decoder_1_output_0, n4_to_16_decoder_1_output_1, n4_to_16_decoder_1_output_2, n4_to_16_decoder_1_output_3, n4_to_16_decoder_1_output_4, n4_to_16_decoder_1_output_7, n4_to_16_decoder_1_output_8, n4_to_16_decoder_1_output_9, n4_to_16_decoder_1_output_10, n4_to_16_decoder_1_output_13);
  not not_2 (CB, nand_2_out);
  nand nand_3 (nand_3_out, n4_to_16_decoder_1_output_0, n4_to_16_decoder_1_output_1, n4_to_16_decoder_1_output_3, n4_to_16_decoder_1_output_4, n4_to_16_decoder_1_output_5, n4_to_16_decoder_1_output_6, n4_to_16_decoder_1_output_7, n4_to_16_decoder_1_output_8, n4_to_16_decoder_1_output_9, n4_to_16_decoder_1_output_10, n4_to_16_decoder_1_output_11, n4_to_16_decoder_1_output_13);
  not not_3 (CC, nand_3_out);
  nand nand_4 (nand_4_out, n4_to_16_decoder_1_output_0, n4_to_16_decoder_1_output_2, n4_to_16_decoder_1_output_3, n4_to_16_decoder_1_output_5, n4_to_16_decoder_1_output_6, n4_to_16_decoder_1_output_8, n4_to_16_decoder_1_output_9, n4_to_16_decoder_1_output_11, n4_to_16_decoder_1_output_12, n4_to_16_decoder_1_output_13, n4_to_16_decoder_1_output_14);
  not not_4 (CD, nand_4_out);
  nand nand_5 (nand_5_out, n4_to_16_decoder_1_output_0, n4_to_16_decoder_1_output_2, n4_to_16_decoder_1_output_6, n4_to_16_decoder_1_output_8, n4_to_16_decoder_1_output_10, n4_to_16_decoder_1_output_11, n4_to_16_decoder_1_output_12, n4_to_16_decoder_1_output_13, n4_to_16_decoder_1_output_14, n4_to_16_decoder_1_output_15);
  not not_5 (CE, nand_5_out);
  nand nand_6 (nand_6_out, n4_to_16_decoder_1_output_0, n4_to_16_decoder_1_output_4, n4_to_16_decoder_1_output_5, n4_to_16_decoder_1_output_6, n4_to_16_decoder_1_output_8, n4_to_16_decoder_1_output_9, n4_to_16_decoder_1_output_10, n4_to_16_decoder_1_output_11, n4_to_16_decoder_1_output_12, n4_to_16_decoder_1_output_14, n4_to_16_decoder_1_output_15);
  not not_6 (CF, nand_6_out);
  nand nand_7 (nand_7_out, n4_to_16_decoder_1_output_2, n4_to_16_decoder_1_output_3, n4_to_16_decoder_1_output_4, n4_to_16_decoder_1_output_5, n4_to_16_decoder_1_output_6, n4_to_16_decoder_1_output_8, n4_to_16_decoder_1_output_9, n4_to_16_decoder_1_output_10, n4_to_16_decoder_1_output_11, n4_to_16_decoder_1_output_13, n4_to_16_decoder_1_output_14, n4_to_16_decoder_1_output_15);
  not not_7 (CG, nand_7_out);
endmodule
