// Logisim project basic_1_graph.circ as structural Verilog: 11 circuits, main circuit BasicQ1
module BasicQ1 (
  input  [2:0] in_1,
  input  A,
  input  B,
  output Output
);

  wire by_nand_2_out, by_nand_3_out, by_nand_4_out, by_nand_5_out, by_nand_6_out, by_nand_out,
       not_by_nand_out;

  not not_by_nand (not_by_nand_out, A);
  nor by_nand (by_nand_out, A, B);
  and by_nand_2 (by_nand_2_out, A, B);
  or by_nand_3 (by_nand_3_out, A, B);
  xor by_nand_4 (by_nand_4_out, A, B);
  xnor by_nand_5 (by_nand_5_out, A, B);
  nand by_nand_6 (by_nand_6_out, A, B);
  Multiplexer #(.select(3), .enable("false")) multiplexer_1 (
    .in0(not_by_nand_out), .in1(by_nand_out), .in2(by_nand_2_out), .in3(by_nand_3_out), .in4(by_nand_4_out),
    .in5(by_nand_5_out), .in6(by_nand_6_out), .in7(by_nand_6_out), .out(Output), .sel(in_1));

  // Notes on the sheet:
  //   NAND_Implement
  //   sel[2:0]
endmodule

module NOT_by_NAND (
  input  A,
  output Output
);

  nand nand_1 (Output, A, A);

  // Notes on the sheet:
  //   NOT gate
endmodule

module AND_by_NAND (
  input  A,
  input  B,
  output Output
);

  wire nand_1_out;

  nand nand_1 (nand_1_out, A, B);
  nand nand_2 (Output, nand_1_out, nand_1_out);

  // Notes on the sheet:
  //   AND gate
endmodule

module OR_by_NAND (
  input  A,
  input  B,
  output Output
);

  wire nand_1_out, nand_2_out;

  nand nand_1 (nand_1_out, A, A);
  nand nand_2 (nand_2_out, B, B);
  nand nand_3 (Output, nand_1_out, nand_2_out);

  // Notes on the sheet:
  //   OR gate
endmodule

module NOR_by_NAND (
  input  A,
  input  B,
  output Output
);

  wire nand_1_out, nand_2_out, nand_3_out;

  nand nand_1 (nand_1_out, A, A);
  nand nand_2 (nand_2_out, B, B);
  nand nand_3 (nand_3_out, nand_1_out, nand_2_out);
  nand nand_4 (Output, nand_3_out, nand_3_out);

  // Notes on the sheet:
  //   NOR gate
endmodule

module NAND_by_NAND (
  input  A,
  input  B,
  output Output
);

  nand nand_1 (Output, A, B);

  // Notes on the sheet:
  //   NAND gate
endmodule

module XOR_by_NAND (
  input  A,
  input  B,
  output Output
);

  wire nand_1_out, nand_2_out, nand_3_out;

  nand nand_1 (nand_1_out, A, B);
  nand nand_2 (nand_2_out, A, nand_1_out);
  nand nand_3 (nand_3_out, nand_1_out, B);
  nand nand_4 (Output, nand_2_out, nand_3_out);

  // Notes on the sheet:
  //   XOR gate
endmodule

module XNOR_by_NAND (
  input  A,
  input  B,
  output Output
);

  wire nand_1_out, nand_2_out, nand_3_out, nand_4_out;

  nand nand_1 (nand_1_out, A, A);
  nand nand_2 (nand_2_out, B, B);
  nand nand_3 (nand_3_out, nand_1_out, nand_2_out);
  nand nand_4 (nand_4_out, A, B);
  nand nand_5 (Output, nand_3_out, nand_4_out);

  // Notes on the sheet:
  //   XNOR gate
endmodule

module _2_to_1_MUX_by_NAND (
  input  sel_1,
  input  in_0,
  input  in_1,
  output Output
);

  wire by_nand_2_out, by_nand_3_out, by_nand_out;

  not by_nand (by_nand_out, sel_1);
  and by_nand_2 (by_nand_2_out, by_nand_out, in_0);
  and by_nand_3 (by_nand_3_out, sel_1, in_1);
  or by_nand_4 (Output, by_nand_2_out, by_nand_3_out);

  // Notes on the sheet:
  //   2 to1 MUX
endmodule

module _8_to_1_MUX_by_NAND (
  input  sel_1,
  input  sel_2,
  input  sel_3,
  input  in_0,
  input  in_1,
  input  in_2,
  input  in_3,
  input  in_4,
  input  in_5,
  input  in_6,
  input  in_7,
  output Output
);

  wire multiplexer_1_out, multiplexer_2_out, multiplexer_3_out, multiplexer_4_out, multiplexer_5_out,
       multiplexer_6_out;

  Multiplexer #(.enable("false")) multiplexer_1 (.in0(in_0), .in1(in_1), .out(multiplexer_1_out), .sel(sel_1));
  Multiplexer #(.enable("false")) multiplexer_2 (.in0(in_2), .in1(in_3), .out(multiplexer_2_out), .sel(sel_1));
  Multiplexer #(.enable("false")) multiplexer_3 (.in0(in_4), .in1(in_5), .out(multiplexer_3_out), .sel(sel_1));
  Multiplexer #(.enable("false")) multiplexer_4 (.in0(in_6), .in1(in_7), .out(multiplexer_4_out), .sel(sel_1));
  Multiplexer #(.enable("false")) multiplexer_5 (
    .in0(multiplexer_1_out), .in1(multiplexer_2_out), .out(multiplexer_5_out), .sel(sel_2));
  Multiplexer #(.enable("false")) multiplexer_6 (
    .in0(multiplexer_3_out), .in1(multiplexer_4_out), .out(multiplexer_6_out), .sel(sel_2));
  Multiplexer #(.enable("false")) multiplexer_7 (
    .in0(multiplexer_5_out), .in1(multiplexer_6_out), .out(Output), .sel(sel_3));

  // Notes on the sheet:
  //   8 to 1MUX
endmodule

module _2_to_1_MUX_by_real_NAND (
  input  sel_1,
  input  in_0,
  input  in_1,
  output Output
);

  wire by_nand_out, nand_1_out, nand_2_out;

  not by_nand (by_nand_out, sel_1);
  nand nand_1 (nand_1_out, by_nand_out, in_0);
  nand nand_2 (nand_2_out, sel_1, in_1);
  nand nand_3 (Output, nand_1_out, nand_2_out);

  // Notes on the sheet:
  //   2 to1 MUX
endmodule
