// Logisim project basic_2_graph.circ as structural Verilog: 11 circuits, main circuit main
module main (
  input  [2:0] sel__2_0,
  input  A,
  input  B,
  output Output
);

  wire by_nor_2_out, by_nor_3_out, by_nor_4_out, by_nor_5_out, by_nor_out, not_by_nand_out;

  not not_by_nand (not_by_nand_out, A);
  nor by_nor (by_nor_out, A, B);
  and by_nor_2 (by_nor_2_out, A, B);
  or by_nor_3 (by_nor_3_out, A, B);
  xor by_nor_4 (by_nor_4_out, A, B);
  xnor by_nor_5 (by_nor_5_out, A, B);
  nand by_nor_6 (by_nor_5_out, A, B);
  Multiplexer #(.select(3), .enable("false")) multiplexer_1 (
    .in0(not_by_nand_out), .in1(by_nor_out), .in2(by_nor_2_out), .in3(by_nor_3_out), .in4(by_nor_4_out),
    .in5(by_nor_5_out), .in6(by_nor_5_out), .in7(by_nor_5_out), .out(Output), .sel(sel__2_0));

  // Notes on the sheet:
  //   NOR_Implement
endmodule

module NOT_by_NOR (
  input  A,
  output Output
);

  nor nor_1 (Output, A, A);

  // Notes on the sheet:
  //   NOT gate
endmodule

module AND_by_NOR (
  input  A,
  input  B,
  output Output
);

  wire nor_1_out, nor_2_out;

  nor nor_1 (nor_1_out, A, A);
  nor nor_2 (nor_2_out, B, B);
  nor nor_3 (Output, nor_1_out, nor_2_out);

  // Notes on the sheet:
  //   AND gate
endmodule

module OR_by_NOR (
  input  A,
  input  B,
  output Output
);

  wire nor_1_out;

  nor nor_1 (nor_1_out, A, B);
  nor nor_2 (Output, nor_1_out, nor_1_out);

  // Notes on the sheet:
  //   OR gate
endmodule

module NAND_by_NOR (
  input  A,
  input  B,
  output Output
);

  wire nor_1_out, nor_2_out, nor_3_out;

  nor nor_1 (nor_1_out, A, A);
  nor nor_2 (nor_2_out, B, B);
  nor nor_3 (nor_3_out, nor_1_out, nor_2_out);
  nor nor_4 (Output, nor_3_out, nor_3_out);

  // Notes on the sheet:
  //   NAND gate
endmodule

module NOR_by_NOR (
  input  A,
  input  B,
  output Output
);

  nor nor_1 (Output, A, B);

  // Notes on the sheet:
  //   NOR gate
endmodule

module XOR_by_NOR (
  input  A,
  input  B,
  output Output
);

  wire nor_1_out, nor_2_out, nor_3_out, nor_4_out;

  nor nor_1 (nor_1_out, A, A);
  nor nor_2 (nor_2_out, B, B);
  nor nor_3 (nor_3_out, A, B);
  nor nor_4 (nor_4_out, nor_1_out, nor_2_out);
  nor nor_5 (Output, nor_3_out, nor_4_out);

  // Notes on the sheet:
  //   XOR gate
endmodule

module XNOR_by_NOR (
  input  A,
  input  B,
  output Output
);

  wire nor_1_out, nor_2_out, nor_3_out;

  nor nor_1 (nor_1_out, A, B);
  nor nor_2 (nor_2_out, A, nor_1_out);
  nor nor_3 (nor_3_out, nor_1_out, B);
  nor nor_4 (Output, nor_2_out, nor_3_out);
  NOT_by_NOR not_by_nor_1 ();  // open: A, Output

  // Notes on the sheet:
  //   XNOR gate
endmodule

module _2_to_1_MUX_by_NOR (
  input  sel,
  input  A,
  input  B,
  output Output
);

  wire by_nand_out, by_nor_2_out, by_nor_out;

  not by_nand (by_nand_out, sel);
  and by_nor (by_nor_out, by_nand_out, A);
  and by_nor_2 (by_nor_2_out, sel, B);
  or by_nor_3 (Output, by_nor_out, by_nor_2_out);

  // Notes on the sheet:
  //   2 to 1 MUX by nor
endmodule

module _8_to_1_MUX_by_NOR (
  input  sel_0,
  input  sel_1,
  input  sel_2,
  input  in_0,
  input  in_1,
  input  in_2,
  input  in_3,
  input  in_4,
  input  in_5,
  input  in_6,
  input  in_7,
  output Output
);

  wire multiplexer_1_out, multiplexer_2_out, multiplexer_3_out, multiplexer_4_out, multiplexer_5_out,
       multiplexer_6_out;

  Multiplexer #(.enable("false")) multiplexer_1 (.in0(in_0), .in1(in_1), .out(multiplexer_1_out), .sel(sel_0));
  Multiplexer #(.enable("false")) multiplexer_2 (.in0(in_2), .in1(in_3), .out(multiplexer_2_out), .sel(sel_0));
  Multiplexer #(.enable("false")) multiplexer_3 (.in0(in_4), .in1(in_5), .out(multiplexer_3_out), .sel(sel_0));
  Multiplexer #(.enable("false")) multiplexer_4 (.in0(in_6), .in1(in_7), .out(multiplexer_4_out), .sel(sel_0));
  Multiplexer #(.enable("false")) multiplexer_5 (
    .in0(multiplexer_1_out), .in1(multiplexer_2_out), .out(multiplexer_5_out), .sel(sel_1));
  Multiplexer #(.enable("false")) multiplexer_6 (
    .in0(multiplexer_3_out), .in1(multiplexer_4_out), .out(multiplexer_6_out), .sel(sel_1));
  Multiplexer #(.enable("false")) multiplexer_7 (
    .in0(multiplexer_5_out), .in1(multiplexer_6_out), .out(Output), .sel(sel_2));

  // Notes on the sheet:
  //   8 to 1MUX
endmodule

module real_mUX (
  input  sel,
  input  A,
  input  B,
  output Output
);

  wire by_nand_out, nor_1_out, nor_2_out;

  not by_nand (by_nand_out, sel);
  nor nor_1 (nor_1_out, sel, A);
  nor nor_2 (nor_2_out, by_nand_out, B);
  nor nor_3 (Output, nor_1_out, nor_2_out);

  // Notes on the sheet:
  //   2 to 1 MUX by nor
endmodule
