// Logisim project AQ1_graph.circ as structural Verilog: 2 circuits, main circuit LFSR
module LFSR (
  input  rst_n,
  output Out
);

  wire clock_1_out, DFF_0_q, DFF_1_q, DFF_2_q, DFF_3_q, multiplexer_1_out, multiplexer_2_out,
       multiplexer_3_out, multiplexer_4_out, multiplexer_5_out, xor_1_out;

  Clock clock_1 (.out(clock_1_out));
  Multiplexer #(.enable("false")) multiplexer_1 (.in0(1'b1), .in1(xor_1_out), .out(multiplexer_1_out), .sel(rst_n));
  D_Flip_Flop DFF_0 (.clk(clock_1_out), .D(multiplexer_1_out), .Q(DFF_0_q));  // open: Qn, preset, en, reset
  Multiplexer #(.enable("false")) multiplexer_2 (.in0(1'b1), .in1(DFF_0_q), .out(multiplexer_2_out), .sel(rst_n));
  xor xor_1 (xor_1_out, DFF_1_q, Out);
  D_Flip_Flop DFF_1 (.clk(clock_1_out), .D(multiplexer_2_out), .Q(DFF_1_q));  // open: Qn, preset, en, reset
  D_Flip_Flop DFF_2 (.clk(clock_1_out), .D(multiplexer_3_out), .Q(DFF_2_q));  // open: Qn, preset, en, reset
  Multiplexer #(.enable("false")) multiplexer_3 (.in0(1'b1), .in1(DFF_1_q), .out(multiplexer_3_out), .sel(rst_n));
  Multiplexer #(.enable("false")) multiplexer_4 (.in0(1'b1), .in1(DFF_2_q), .out(multiplexer_4_out), .sel(rst_n));
  D_Flip_Flop DFF_3 (.clk(clock_1_out), .D(multiplexer_4_out), .Q(DFF_3_q));  // open: Qn, preset, en, reset
  Multiplexer #(.enable("false")) multiplexer_5 (.in0(1'b1), .in1(DFF_3_q), .out(multiplexer_5_out), .sel(rst_n));
  D_Flip_Flop DFF_4 (.clk(clock_1_out), .D(multiplexer_5_out), .Q(Out));  // open: Qn, preset, en, reset
endmodule

module LFSR_lookinside (
  input  rst_n,
  output Out,
  output DFF_out_0,
  output DFF_out_1,
  output DFF_out_2,
  output DFF_out_3,
  output DFF_out_4
);

  wire clock_1_out, multiplexer_1_out, multiplexer_2_out, multiplexer_3_out, multiplexer_4_out,
       multiplexer_5_out, xor_1_out;

  Clock clock_1 (.out(clock_1_out));
  Multiplexer #(.enable("false")) multiplexer_1 (.in0(1'b1), .in1(xor_1_out), .out(multiplexer_1_out), .sel(rst_n));
  D_Flip_Flop DFF_0 (.clk(clock_1_out), .D(multiplexer_1_out), .Q(DFF_out_0));  // open: Qn, preset, en, reset
  Multiplexer #(.enable("false")) multiplexer_2 (.in0(1'b1), .in1(DFF_out_0), .out(multiplexer_2_out), .sel(rst_n));
  xor xor_1 (xor_1_out, DFF_out_1, DFF_out_4);
  D_Flip_Flop DFF_1 (.clk(clock_1_out), .D(multiplexer_2_out), .Q(DFF_out_1));  // open: Qn, preset, en, reset
  Multiplexer #(.enable("false")) multiplexer_3 (.in0(1'b1), .in1(DFF_out_1), .out(multiplexer_3_out), .sel(rst_n));
  D_Flip_Flop DFF_2 (.clk(clock_1_out), .D(multiplexer_3_out), .Q(DFF_out_2));  // open: Qn, preset, en, reset
  D_Flip_Flop DFF_3 (.clk(clock_1_out), .D(multiplexer_4_out), .Q(DFF_out_3));  // open: Qn, preset, en, reset
  Multiplexer #(.enable("false")) multiplexer_4 (.in0(1'b1), .in1(DFF_out_2), .out(multiplexer_4_out), .sel(rst_n));
  Multiplexer #(.enable("false")) multiplexer_5 (.in0(1'b1), .in1(DFF_out_3), .out(multiplexer_5_out), .sel(rst_n));
  D_Flip_Flop DFF_4 (.clk(clock_1_out), .D(multiplexer_5_out), .Q(DFF_out_4));  // open: Qn, preset, en, reset

  assign Out = DFF_out_4;
endmodule
