// Logisim project AQ2_graph.circ as structural Verilog: 1 circuit, main circuit main
module main (
  input  [6:0] addr,
  input  [7:0] din,
  input  wen,
  input  ren,
  output [7:0] dout
);

  wire clk_out;
  wire [7:0] multiplexer_1_out, multiplexer_2_out, ram_1_data;

  Multiplexer #(.select(2), .width(8), .enable("false")) multiplexer_1 (
    .in0(ram_1_data), .in1(din), .in2(ram_1_data), .in3(ram_1_data), .out(multiplexer_1_out), .sel({ren, wen}));
  Clock clk (.out(clk_out));
  RAM #(.addrWidth(7), .bus("separate")) ram_1 (
    .addr(addr), .din(multiplexer_1_out), .data(ram_1_data), .clk(clk_out));  // open: str, sel, ld, clr
  Multiplexer #(.select(2), .width(8), .enable("false")) multiplexer_2 (
    .in0({8{1'b0}}), .in1({8{1'b0}}), .in2(ram_1_data), .in3(ram_1_data), .out(multiplexer_2_out),
    .sel({ren, wen}));
  Register data (.D(multiplexer_2_out), .Q(dout), .clk(clk_out));  // open: en, clr
endmodule
