// Logisim project AQ1_graph.circ as structural Verilog
module _8bitMEM (
  input  in_1
);

  wire clock_1_out;

  Clock clock_1 (.out(clock_1_out));
  D_Flip_Flop d_ff_1 (.clk(clock_1_out), .D(in_1));  // open: Q, Qn, preset, en, reset
endmodule
